// Logisim project ORT_Praktikum_domaci_1.circ as structural Verilog: 1 circuit, main circuit Slika_1
module Slika_1 (
  input  x1,
  input  x2,
  output Y
);

  wire nor_1_out, not_1_out;

  not not_1 (not_1_out, x1);
  // Probe on nor_1_out
  nor nor_1 (nor_1_out, x2, x1);
  and and_1 (Y, nor_1_out, not_1_out);
  // Probe on Y
endmodule
